# Fritzing sketch NFC_Breadboard_Schaltung (saved by Fritzing 0.8.7b)
breadboards: 1

parts:
  Bauteil1 = Arduino Nano (Rev3.0) (ICSP)
  S1 = Pushbutton [package="[THT]"]
  S2 = Pushbutton [package="[THT]"]
  R1 = Resistor [tolerance=±5% resistance=10k package=THT]
  R2 = Resistor [tolerance=±5% resistance=10k package=THT]
  Bauteil2 = Bluetooth HC-05 Macho
  Bauteil3 = RFID-RC522-v2
  R3 = Resistor [tolerance=±5% resistance=1k package=THT]
  R4 = Resistor [tolerance=±5% resistance=1k package=THT]

nets:
  GND: Bauteil1.GND, S1.Pin_3, S1.Pin_4, S2.Pin_3, S2.Pin_4, Bauteil2.GND, Bauteil3.GND, R3.Pin_1
  N1: Bauteil1.D2, S2.Pin_1, S2.Pin_2, R2.Pin_0
  N2: Bauteil1.D3, S1.Pin_1, S1.Pin_2, R1.Pin_1
  N3: Bauteil1.D7, Bauteil2.RXD
  N4: Bauteil1.D8, R4.Pin_0
  N5: Bauteil1.D9, Bauteil3.RST
  N6: Bauteil1.D10, Bauteil3.SDA
  N7: Bauteil1.D11/MOSI, Bauteil3.MISO
  N8: Bauteil1.D12/MISO, Bauteil3.MOSI
  5V: Bauteil1.5V, R1.Pin_0, R2.Pin_1, Bauteil2.VCC
  3V3: Bauteil1.3V3, Bauteil3.3.3V
  N9: Bauteil1.D13/SCK, Bauteil3.SCK
  N10: Bauteil2.TXD, R3.Pin_0, R4.Pin_1

custom parts:
  RFID-RC522-v2: A simple China made RFID-RC522 Reader; do check the pin labels, as this is a MFRC522 based clone.
