# Fritzing sketch NFC_schaltung (saved by Fritzing 0.8.7b)
stripboards: 2

parts:
  Bauteil1 = Arduino Nano (Rev3.0)
  S1 = Pushbutton [package="[THT]"]
  S2 = Pushbutton [package="[THT]"]
  Bauteil2 = Bluetooth HC-05 Macho
  R2 = Resistor [tolerance=±5% resistance=10k package=THT]
  R3 = Resistor [tolerance=±5% resistance=1k package=THT]
  R4 = Resistor [tolerance=±5% resistance=2.2k package=THT]
  R5 = Resistor [tolerance=±5% resistance=10k package=THT]
  Bauteil3 = RFID-RC522-v2

nets:
  GND: Bauteil1.GND, S1.Pin_1, S1.Pin_2, S2.Pin_1, S2.Pin_2, Bauteil2.GND, R3.Pin_0, Bauteil3.GND
  N1: Bauteil1.D2, S1.Pin_3, S1.Pin_4, R2.Pin_0
  5V: Bauteil1.D3, Bauteil1.5V, S2.Pin_3, S2.Pin_4, Bauteil2.VCC, R2.Pin_1, R5.Pin_0, R5.Pin_1
  N2: Bauteil1.D7, Bauteil2.TXD
  N3: Bauteil1.D8, R4.Pin_0
  N4: Bauteil1.D9, Bauteil3.RST
  N5: Bauteil1.D10, Bauteil3.SDA
  N6: Bauteil1.D11/MOSI, Bauteil3.MISO
  N7: Bauteil1.D12/MISO, Bauteil3.MOSI
  3V3: Bauteil1.3V3, Bauteil3.3.3V
  N8: Bauteil1.D13/SCK, Bauteil3.SCK
  N9: Bauteil2.RXD, R3.Pin_1, R4.Pin_1

custom parts:
  RFID-RC522-v2: A simple China made RFID-RC522 Reader; do check the pin labels, as this is a MFRC522 based clone.
